// Logisim project MIPS.circ as structural Verilog: 6 circuits, main circuit main
module main (
  input  in_1
);

  wire clock, control_1_alu_src, control_1_branch, control_1_jump, control_1_link, control_1_mem_read,
       control_1_mem_to_reg, control_1_mem_write, control_1_reg_write, control_1_return_address, flush,
       mem_read, mem_write, reg_dst, reg_write, register_3_q, register_4_q, register_9_q, register_10_q,
       register_11_q, register_14_q, register_18_q;
  wire [1:0] control_1_alu_op, register_12_q;
  wire [3:0] alucontol_1_alu_control_signal;
  wire [4:0] multiplexer_1_out, register_7_q, register_16_q, write_reg_wb;
  wire [5:0] sign_extended_0_5;
  wire [15:0] bit_extender_2_out;
  wire [23:0] bit_extender_1_out, bit_extender_4_out;
  wire [31:0] adder_1_out, alu_1_alu_out, jump_branch_handle_1_pc, multiplexer_2_out, pc_q, ram_1_data,
       ram_2_data, read_data_1, read_data_1_exe, read_data_2, read_data_2_exe, register_1_q, register_2_q,
       register_15_q, register_19_q, register_22_q, register_23_q, sign_extended, write_data_wb;
  wire [31:6] sign_extended_exe;

  Register #(.width(32)) pc (.D(jump_branch_handle_1_pc), .Q(pc_q), .clk(clock), .clr(in_1));  // open: en
  Clock clock_1 (.out(clock));
  Bit_Extender #(.in_width(32), .out_width(24)) bit_extender_1 (.in(pc_q), .out(bit_extender_1_out));
  Adder #(.width(32)) adder_1 (.a(pc_q), .b(32'h1), .out(adder_1_out));  // open: cin, cout
  Register #(.width(32)) register_1 (.D(ram_1_data), .Q(register_1_q), .clk(clock), .clr(flush));  // open: en
  RAM #(.addrWidth(24), .dataWidth(32)) ram_1 (
    .addr(bit_extender_1_out), .data(ram_1_data));  // open: sel, clk, ld, clr
  Register #(.width(32)) register_2 (.D(adder_1_out), .Q(register_2_q), .clk(clock));  // open: en, clr
  control control_1 (
    .opcode(register_1_q[31:26]), .reg_dst(reg_dst), .jump(control_1_jump), .branch(control_1_branch),
    .mem_read(control_1_mem_read), .mem_to_reg(control_1_mem_to_reg), .mem_write(control_1_mem_write),
    .alu_src(control_1_alu_src), .reg_write(control_1_reg_write), .link(control_1_link),
    .return_address(control_1_return_address), .alu_op(control_1_alu_op));
  Multiplexer #(.width(5), .enable("false")) multiplexer_1 (
    .in0(register_1_q[20:16]), .in1(register_1_q[15:11]), .out(multiplexer_1_out), .sel(reg_dst));
  Bit_Extender #(.in_width(32)) bit_extender_2 (.in(register_1_q), .out(bit_extender_2_out));
  jump_branch_handle jump_branch_handle_1 (
    .pc_4(register_2_q), .sign_extended(sign_extended), .instruction(register_1_q),
    .read_data_1(read_data_1), .read_data_2(read_data_2), .branch(control_1_branch), .jump(control_1_jump),
    .link(control_1_link), .\return (control_1_return_address), .pc(jump_branch_handle_1_pc), .flush(flush));
  assign sign_extended = {{16{bit_extender_2_out[15]}}, bit_extender_2_out};  // Bit_Extender bit_extender_3
  registers registers_1 (
    .read_reg_1(register_1_q[25:21]), .read_reg_2(register_1_q[20:16]), .write_reg(write_reg_wb),
    .write_data(write_data_wb), .reg_write(reg_write), .read_data_1(read_data_1), .read_data_2(read_data_2));  // open: out_7
  Register #(.width(1)) register_3 (.D(control_1_mem_read), .Q(register_3_q), .clk(clock));  // open: en, clr
  Register #(.width(1)) register_4 (.D(control_1_mem_to_reg), .Q(register_4_q), .clk(clock));  // open: en, clr
  Register #(.width(32)) register_5 (.D(read_data_1), .Q(read_data_1_exe), .clk(clock));  // open: en, clr
  Register #(.width(32)) register_6 (.D(read_data_2), .Q(read_data_2_exe), .clk(clock));  // open: en, clr
  Register #(.width(5)) register_7 (.D(multiplexer_1_out), .Q(register_7_q), .clk(clock));  // open: en, clr
  Register #(.width(32)) register_8 (
    .D(sign_extended), .Q({sign_extended_exe, sign_extended_0_5}), .clk(clock));  // open: en, clr
  Register #(.width(1)) register_9 (.D(control_1_mem_write), .Q(register_9_q), .clk(clock));  // open: en, clr
  Register #(.width(1)) register_10 (.D(control_1_alu_src), .Q(register_10_q), .clk(clock));  // open: en, clr
  Register #(.width(1)) register_11 (.D(control_1_reg_write), .Q(register_11_q), .clk(clock));  // open: en, clr
  Register #(.width(2)) register_12 (.D(control_1_alu_op), .Q(register_12_q), .clk(clock));  // open: en, clr
  Register #(.width(1)) register_13 (.D(register_3_q), .Q(mem_read), .clk(clock));  // open: en, clr
  Register #(.width(1)) register_14 (.D(register_4_q), .Q(register_14_q), .clk(clock));  // open: en, clr
  ALU alu_1 (
    .reg1(read_data_1_exe), .reg2(multiplexer_2_out), .alu_control_signal(alucontol_1_alu_control_signal),
    .alu_out(alu_1_alu_out));
  Multiplexer #(.width(32), .enable("false")) multiplexer_2 (
    .in0(read_data_2_exe), .in1({sign_extended_exe, sign_extended_0_5}), .out(multiplexer_2_out),
    .sel(register_10_q));
  alucontol alucontol_1 (
    .alu_op(register_12_q), .in_2(sign_extended_0_5), .alu_control_signal(alucontol_1_alu_control_signal));
  Register #(.width(32)) register_15 (.D(read_data_2_exe), .Q(register_15_q), .clk(clock));  // open: en, clr
  Register #(.width(5)) register_16 (.D(register_7_q), .Q(register_16_q), .clk(clock));  // open: en, clr
  Register #(.width(1)) register_17 (.D(register_9_q), .Q(mem_write), .clk(clock));  // open: en, clr
  Register #(.width(1)) register_18 (.D(register_11_q), .Q(register_18_q), .clk(clock));  // open: en, clr
  Register #(.width(32)) register_19 (.D(alu_1_alu_out), .Q(register_19_q), .clk(clock));  // open: en, clr
  Bit_Extender #(.in_width(32), .out_width(24)) bit_extender_4 (.in(register_19_q), .out(bit_extender_4_out));
  Register #(.width(1)) register_20 (.D(register_18_q), .Q(reg_write), .clk(clock));  // open: en, clr
  RAM #(.addrWidth(24), .dataWidth(32), .bus("separate")) ram_2 (
    .addr(bit_extender_4_out), .din(register_15_q), .data(ram_2_data), .str(mem_write), .clk(clock),
    .ld(mem_read));  // open: sel, clr
  Register #(.width(5)) register_21 (.D(register_16_q), .Q(write_reg_wb), .clk(clock));  // open: en, clr
  Register #(.width(32)) register_22 (.D(register_19_q), .Q(register_22_q), .clk(clock));  // open: en, clr
  Register #(.width(32)) register_23 (.D(ram_2_data), .Q(register_23_q), .clk(clock));  // open: en, clr
  Multiplexer #(.width(32), .enable("false")) multiplexer_3 (
    .in0(register_22_q), .in1(register_23_q), .out(write_data_wb), .sel(register_14_q));

  // Other names for the same wires on the sheet: sign_extended_exe[5:0] = sign_extended_0_5
endmodule

module ALU (
  input  [31:0] reg1,
  input  [31:0] reg2,
  input  [3:0] alu_control_signal,
  output [31:0] alu_out
);

  wire comparator_1_lt;
  wire [4:0] bit_extender_1_out;
  wire [31:0] add, \and , \nor , \or , sll, slt, sub;

  Bit_Extender #(.in_width(32), .out_width(5)) bit_extender_1 (.in(reg2), .out(bit_extender_1_out));
  assign \and  = reg1 & reg2;  // AND_Gate and_1, 32 bits wide
  assign \or  = reg1 | reg2;  // OR_Gate or_1, 32 bits wide
  Adder #(.width(32)) adder_1 (.a(reg1), .b(reg2), .out(add));  // open: cin, cout
  Shifter #(.width(32)) shifter_1 (.in(reg1), .\dist (bit_extender_1_out), .out(sll));
  Subtractor #(.width(32)) subtractor_1 (.a(reg1), .b(reg2), .out(sub));  // open: bin, bout
  Comparator #(.width(32)) comparator_1 (.a(reg1), .b(reg2), .lt(comparator_1_lt));  // open: gt, eq
  assign slt = {{31{1'b0}}, comparator_1_lt};  // Bit_Extender bit_extender_2
  assign \nor  = ~(reg1 | reg2);  // NOR_Gate nor_1, 32 bits wide
  Multiplexer #(.select(4), .width(32), .enable("false")) multiplexer_1 (
    .in0(\and ), .in1(\or ), .in2(add), .in3(sll), .in6(sub), .in7(slt), .in12(\nor ), .out(alu_out),
    .sel(alu_control_signal));  // open: in4, in5, in8, in9, in10, in11, in13, in14, in15

  // Other names for the same wires on the sheet: rega[31:0] = reg1; regb[31:0] = reg2
endmodule

module alucontol (
  input  [1:0] alu_op,
  input  [5:0] in_2,
  output [3:0] alu_control_signal
);

  wire add0, add1, and_3_out, and_4_out, and_5_out, and_6_out, and_7_out, and_8_out, and_9_out, enc0, enc1,
       enc2, enc3, enc6, enc7, enc12, sub0, sub1;

  and and_1 (add0, ~alu_op[0], ~alu_op[1]);  // AND_Gate
  and and_2 (sub0, alu_op[0], ~alu_op[1]);  // AND_Gate
  and and_3 (and_3_out, ~in_2[0], ~in_2[1], ~in_2[2], ~in_2[3], ~in_2[4], in_2[5]);  // AND_Gate
  and and_4 (and_4_out, ~in_2[0], in_2[1], ~in_2[2], ~in_2[3], ~in_2[4], in_2[5]);  // AND_Gate
  and and_5 (and_5_out, ~in_2[0], ~in_2[1], in_2[2], ~in_2[3], ~in_2[4], in_2[5]);  // AND_Gate
  and and_6 (and_6_out, in_2[0], ~in_2[1], in_2[2], ~in_2[3], ~in_2[4], in_2[5]);  // AND_Gate
  and and_7 (and_7_out, ~in_2[0], in_2[1], ~in_2[2], in_2[3], ~in_2[4], in_2[5]);  // AND_Gate
  and and_8 (and_8_out, in_2[0], in_2[1], in_2[2], ~in_2[3], ~in_2[4], in_2[5]);  // AND_Gate
  and and_9 (and_9_out, ~in_2[0], ~in_2[1], ~in_2[2], ~in_2[3], ~in_2[4], ~in_2[5]);  // AND_Gate
  and and_10 (add1, and_3_out, alu_op[1]);
  and and_11 (sub1, and_4_out, alu_op[1]);
  and and_12 (enc0, and_5_out, alu_op[1]);
  and and_13 (enc1, and_6_out, alu_op[1]);
  and and_14 (enc7, and_7_out, alu_op[1]);
  and and_15 (enc12, and_8_out, alu_op[1]);
  and and_16 (enc3, and_9_out, alu_op[1]);
  or or_1 (enc2, add0, add1);
  or or_2 (enc6, sub0, sub1);
  Priority_Encoder #(.select(4)) priority_encoder_1 (
    .in0(enc0), .in1(enc1), .in2(enc2), .in3(enc3), .in6(enc6), .in7(enc7), .in12(enc12),
    .out(alu_control_signal), .en_in(1'b1));  // open: in4, in5, in8, in9, in10, in11, in13, in14, in15, gs, en_out

  // Other names for the same wires on the sheet: op0 = alu_op[0]; op1 = alu_op[1]; funct0 = in_2[0]; funct1 = in_2[1];
  //   funct2 = in_2[2]; funct3 = in_2[3]; funct4 = in_2[4]; funct5 = in_2[5]
endmodule

module control (
  input  [5:0] opcode,
  output reg_dst,
  output jump,
  output branch,
  output mem_read,
  output mem_to_reg,
  output mem_write,
  output alu_src,
  output reg_write,
  output link,
  output return_address,
  output [1:0] alu_op
);

  wire and_6_out, and_7_out;

  and and_1 (reg_dst, ~opcode[0], ~opcode[1], ~opcode[2], ~opcode[3], ~opcode[4], ~opcode[5]);  // AND_Gate
  and and_2 (jump, opcode[1], ~opcode[3], ~opcode[4], ~opcode[5]);  // AND_Gate
  and and_3 (branch, ~opcode[0], ~opcode[1], opcode[2], ~opcode[3], ~opcode[4], ~opcode[5]);  // AND_Gate
  and and_4 (mem_read, opcode[0], opcode[1], ~opcode[2], ~opcode[3], ~opcode[4], opcode[5]);  // AND_Gate
  and and_5 (mem_write, opcode[0], opcode[1], ~opcode[2], opcode[3], ~opcode[4], opcode[5]);  // AND_Gate
  and and_6 (and_6_out, ~opcode[0], ~opcode[1], ~opcode[2], opcode[3], ~opcode[4], ~opcode[5]);  // AND_Gate
  and and_7 (and_7_out, ~opcode[0], ~opcode[1], ~opcode[2], opcode[3], ~opcode[4], ~opcode[5]);  // AND_Gate
  and and_8 (link, opcode[0], opcode[1], ~opcode[2], ~opcode[3], ~opcode[4], ~opcode[5]);  // AND_Gate
  and and_9 (return_address, opcode[0], opcode[1], opcode[2], ~opcode[3], ~opcode[4], ~opcode[5]);  // AND_Gate
  or or_1 (alu_src, mem_read, and_6_out, mem_write);
  or or_2 (reg_write, mem_read, and_7_out, reg_dst);
  Priority_Encoder #(.select(2)) priority_encoder_1 (
    .in0(1'b1), .in1(branch), .in2(reg_dst), .out(alu_op), .en_in(1'b1));  // open: in3, gs, en_out

  assign mem_to_reg = mem_read;

  // Other names for the same wires on the sheet: op0 = opcode[0]; op1 = opcode[1]; op2 = opcode[2]; op3 = opcode[3];
  //   op4 = opcode[4]; op5 = opcode[5]
endmodule

module registers (
  input  reg_write,
  input  [4:0] read_reg_1,
  input  [4:0] read_reg_2,
  input  [4:0] write_reg,
  input  [31:0] write_data,
  output [31:0] read_data_1,
  output [31:0] out_7,
  output [31:0] read_data_2
);

  wire reg_write_0, reg_write_1, reg_write_2, reg_write_3, reg_write_4, reg_write_5, reg_write_6,
       reg_write_7, reg_write_8, reg_write_9, reg_write_10, reg_write_11, reg_write_12, reg_write_13,
       reg_write_14, reg_write_15, reg_write_16, reg_write_17, reg_write_18, reg_write_19, reg_write_20,
       reg_write_21, reg_write_22, reg_write_23, reg_write_24, reg_write_25, reg_write_26, reg_write_27,
       reg_write_28, reg_write_29, reg_write_30, reg_write_31;
  wire [31:0] reg0, reg1, reg2, reg3, reg5, reg6, reg7, reg8, reg9, reg10, reg11, reg12, reg13, reg14, reg15,
       reg16, reg17, reg18, reg19, reg20, reg21, reg22, reg23, reg24, reg25, reg26, reg27, reg28, reg29,
       reg30, reg31;

  Decoder #(.select(5), .enable("false")) decoder_1 (
    .out0(reg_write_0), .out1(reg_write_1), .out2(reg_write_2), .out3(reg_write_3), .out4(reg_write_4),
    .out5(reg_write_5), .out6(reg_write_6), .out7(reg_write_7), .out8(reg_write_8), .out9(reg_write_9),
    .out10(reg_write_10), .out11(reg_write_11), .out12(reg_write_12), .out13(reg_write_13),
    .out14(reg_write_14), .out15(reg_write_15), .out16(reg_write_16), .out17(reg_write_17),
    .out18(reg_write_18), .out19(reg_write_19), .out20(reg_write_20), .out21(reg_write_21),
    .out22(reg_write_22), .out23(reg_write_23), .out24(reg_write_24), .out25(reg_write_25),
    .out26(reg_write_26), .out27(reg_write_27), .out28(reg_write_28), .out29(reg_write_29),
    .out30(reg_write_30), .out31(reg_write_31), .sel(write_reg));
  Multiplexer #(.select(5), .width(32), .enable("false")) multiplexer_1 (
    .in0(reg0), .in1(reg1), .in2(reg2), .in3(reg3), .in4(out_7), .in5(reg5), .in6(reg6), .in7(reg7),
    .in8(reg8), .in9(reg9), .in10(reg10), .in11(reg11), .in12(reg12), .in13(reg13), .in14(reg14),
    .in15(reg15), .in16(reg16), .in17(reg17), .in18(reg18), .in19(reg19), .in20(reg20), .in21(reg21),
    .in22(reg22), .in23(reg23), .in24(reg24), .in25(reg25), .in26(reg26), .in27(reg27), .in28(reg28),
    .in29(reg29), .in30(reg30), .in31(reg31), .out(read_data_1), .sel(read_reg_1));
  Multiplexer #(.select(5), .width(32), .enable("false")) multiplexer_2 (
    .in0(reg0), .in1(reg1), .in2(reg2), .in3(reg3), .in4(out_7), .in5(reg5), .in6(reg6), .in7(reg7),
    .in8(reg8), .in9(reg9), .in10(reg10), .in11(reg11), .in12(reg12), .in13(reg13), .in14(reg14),
    .in15(reg15), .in16(reg16), .in17(reg17), .in18(reg18), .in19(reg19), .in20(reg20), .in21(reg21),
    .in22(reg22), .in23(reg23), .in24(reg24), .in25(reg25), .in26(reg26), .in27(reg27), .in28(reg28),
    .in29(reg29), .in30(reg30), .in31(reg31), .out(read_data_2), .sel(read_reg_2));
  Register #(.width(32), .trigger("high")) register_1 (
    .D(write_data), .en(reg_write_0), .Q(reg0), .clk(reg_write));  // open: clr
  Register #(.width(32), .trigger("high")) register_2 (
    .D(write_data), .en(reg_write_1), .Q(reg1), .clk(reg_write));  // open: clr
  Register #(.width(32), .trigger("high")) register_3 (
    .D(write_data), .en(reg_write_2), .Q(reg2), .clk(reg_write));  // open: clr
  Register #(.width(32), .trigger("high")) register_4 (
    .D(write_data), .en(reg_write_3), .Q(reg3), .clk(reg_write));  // open: clr
  Register #(.width(32), .trigger("high")) register_5 (
    .D(write_data), .en(reg_write_4), .Q(out_7), .clk(reg_write));  // open: clr
  Register #(.width(32), .trigger("high")) register_6 (
    .D(write_data), .en(reg_write_5), .Q(reg5), .clk(reg_write));  // open: clr
  Register #(.width(32), .trigger("high")) register_7 (
    .D(write_data), .en(reg_write_6), .Q(reg6), .clk(reg_write));  // open: clr
  Register #(.width(32), .trigger("high")) register_8 (
    .D(write_data), .en(reg_write_7), .Q(reg7), .clk(reg_write));  // open: clr
  Register #(.width(32), .trigger("high")) register_9 (
    .D(write_data), .en(reg_write_8), .Q(reg8), .clk(reg_write));  // open: clr
  Register #(.width(32), .trigger("high")) register_10 (
    .D(write_data), .en(reg_write_9), .Q(reg9), .clk(reg_write));  // open: clr
  Register #(.width(32), .trigger("high")) register_11 (
    .D(write_data), .en(reg_write_10), .Q(reg10), .clk(reg_write));  // open: clr
  Register #(.width(32), .trigger("high")) register_12 (
    .D(write_data), .en(reg_write_11), .Q(reg11), .clk(reg_write));  // open: clr
  Register #(.width(32), .trigger("high")) register_13 (
    .D(write_data), .en(reg_write_12), .Q(reg12), .clk(reg_write));  // open: clr
  Register #(.width(32), .trigger("high")) register_14 (
    .D(write_data), .en(reg_write_13), .Q(reg13), .clk(reg_write));  // open: clr
  Register #(.width(32), .trigger("high")) register_15 (
    .D(write_data), .en(reg_write_14), .Q(reg14), .clk(reg_write));  // open: clr
  Register #(.width(32), .trigger("high")) register_16 (
    .D(write_data), .en(reg_write_15), .Q(reg15), .clk(reg_write));  // open: clr
  Register #(.width(32), .trigger("high")) register_17 (
    .D(write_data), .en(reg_write_16), .Q(reg16), .clk(reg_write));  // open: clr
  Register #(.width(32), .trigger("high")) register_18 (
    .D(write_data), .en(reg_write_17), .Q(reg17), .clk(reg_write));  // open: clr
  Register #(.width(32), .trigger("high")) register_19 (
    .D(write_data), .en(reg_write_18), .Q(reg18), .clk(reg_write));  // open: clr
  Register #(.width(32), .trigger("high")) register_20 (
    .D(write_data), .en(reg_write_19), .Q(reg19), .clk(reg_write));  // open: clr
  Register #(.width(32), .trigger("high")) register_21 (
    .D(write_data), .en(reg_write_20), .Q(reg20), .clk(reg_write));  // open: clr
  Register #(.width(32), .trigger("high")) register_22 (
    .D(write_data), .en(reg_write_21), .Q(reg21), .clk(reg_write));  // open: clr
  Register #(.width(32), .trigger("high")) register_23 (
    .D(write_data), .en(reg_write_22), .Q(reg22), .clk(reg_write));  // open: clr
  Register #(.width(32), .trigger("high")) register_24 (
    .D(write_data), .en(reg_write_23), .Q(reg23), .clk(reg_write));  // open: clr
  Register #(.width(32), .trigger("high")) register_25 (
    .D(write_data), .en(reg_write_24), .Q(reg24), .clk(reg_write));  // open: clr
  Register #(.width(32), .trigger("high")) register_26 (
    .D(write_data), .en(reg_write_25), .Q(reg25), .clk(reg_write));  // open: clr
  Register #(.width(32), .trigger("high")) register_27 (
    .D(write_data), .en(reg_write_26), .Q(reg26), .clk(reg_write));  // open: clr
  Register #(.width(32), .trigger("high")) register_28 (
    .D(write_data), .en(reg_write_27), .Q(reg27), .clk(reg_write));  // open: clr
  Register #(.width(32), .trigger("high")) register_29 (
    .D(write_data), .en(reg_write_28), .Q(reg28), .clk(reg_write));  // open: clr
  Register #(.width(32), .trigger("high")) register_30 (
    .D(write_data), .en(reg_write_29), .Q(reg29), .clk(reg_write));  // open: clr
  Register #(.width(32), .trigger("high")) register_31 (
    .D(write_data), .en(reg_write_30), .Q(reg30), .clk(reg_write));  // open: clr
  Register #(.width(32), .trigger("high")) register_32 (
    .D(write_data), .en(reg_write_31), .Q(reg31), .clk(reg_write));  // open: clr

  // Other names for the same wires on the sheet: reg4[31:0] = out_7
endmodule

module jump_branch_handle (
  input  [31:0] pc_4,
  input  [31:0] sign_extended,
  input  [31:0] instruction,
  input  [31:0] read_data_1,
  input  [31:0] read_data_2,
  input  branch,
  input  jump,
  input  link,
  input  \return ,
  output [31:0] pc,
  output flush
);

  wire branch_t, comparator_1_eq;
  wire [25:0] instruction_t;
  wire [31:0] branch_address, jump_address, multiplexer_2_out, ra;

  Bit_Extender #(.in_width(32), .out_width(26)) bit_extender_1 (.in(instruction), .out(instruction_t));
  and and_1 (branch_t, branch, comparator_1_eq);
  Comparator #(.width(32)) comparator_1 (.a(read_data_1), .b(read_data_2), .eq(comparator_1_eq));  // open: gt, lt
  Adder #(.width(32)) adder_1 (.a(pc_4), .b(sign_extended), .out(branch_address));  // open: cin, cout
  Multiplexer #(.width(32), .enable("false")) multiplexer_1 (
    .in0({pc_4[31:26], instruction_t}), .in1(ra), .out(jump_address), .sel(\return ));
  Register #(.width(32), .trigger("high")) u_ra (.D(pc_4), .en(link), .Q(ra), .clk(1'b1));  // open: clr
  Multiplexer #(.width(32), .enable("false")) multiplexer_2 (
    .in0(pc_4), .in1(branch_address), .out(multiplexer_2_out), .sel(branch_t));
  or or_1 (flush, branch_t, jump);
  Multiplexer #(.width(32), .enable("false")) multiplexer_3 (
    .in0(multiplexer_2_out), .in1(jump_address), .out(pc), .sel(jump));

  // Other names for the same wires on the sheet: sign_extend[31:0] = sign_extended
endmodule
